// Logisim project zaid.circ as structural Verilog: 8 circuits, main circuit main
module main (
  input  in_1,
  input  in_2,
  output [31:0] out_3,
  output [31:0] out_4
);

  wire alu_1_p5, button_1_out, clock_1_out, control_decoder_1_regwrite;
  wire [4:0] control_decoder_1_rd, control_decoder_1_rs1, control_decoder_1_rs2;
  wire [5:0] control_decoder_1_aluop;
  wire [31:0] adder_1_out, data_memory_interface_1_store_data, register_1_q, rom_1_data;

  Register #(.width(32)) register_1 (
    .D(adder_1_out), .en(in_1), .Q(register_1_q), .clk(clock_1_out), .clr(button_1_out));
  Clock clock_1 (.out(clock_1_out));
  // Probe on register_1_q
  Button button_1 (.out(button_1_out));
  Adder #(.width(32)) adder_1 (.a(register_1_q), .b(32'h4), .out(adder_1_out));  // open: cin, cout
  // Probe on rom_1_data
  ROM #(.addrWidth(24), .dataWidth(32)) rom_1 (.addr(register_1_q[25:2]), .data(rom_1_data), .sel(in_2));
  Control_Decoder control_decoder_1 (
    ._32bit_instruction(rom_1_data), .rd(control_decoder_1_rd), .rs1(control_decoder_1_rs1),
    .rs2(control_decoder_1_rs2), ._32bit_immediate(out_4), .regWrite(control_decoder_1_regwrite),
    .aluOP(control_decoder_1_aluop));  // open: mem_to_reg, mem_write, operand_a, operand_b, branch
  _32_bit_reg_reg_file u_32_bit_reg_reg_file_1 (
    .write_data(rom_1_data), .writeReg(control_decoder_1_regwrite),
    .destination_register(control_decoder_1_rd), .read_register_1(control_decoder_1_rs1),
    .read_register_2(control_decoder_1_rs2), .reset(button_1_out), .read_data_1(out_4), .read_data_2(out_3),
    .clock(clock_1_out));
  // alu alu_1: pin names not known; wires that end beside it: out_4, out_3, adder_1_out, control_decoder_1_aluop, alu_1_p5
  data_memory_interface data_memory_interface_1 (
    .aluOP(control_decoder_1_aluop), .RS2(out_3), .STORE_DATA(data_memory_interface_1_store_data));
  RAM #(.addrWidth(24), .dataWidth(32), .bus("separate")) ram_1 (.clk(clock_1_out));  // open: addr, din, data, str, sel, ld, clr

  // Notes on the sheet:
  //   contents of rom_1 (hex, n*v repeats v):
  //   11000011 11000001 10111011 1101001 1100110 10001010 10011001 1010101
endmodule

module decoder (
  input  [31:0] _32_bit_instructions,
  output [6:0] opcode,
  output [4:0] rd,
  output [2:0] func_3,
  output [4:0] rs1,
  output [4:0] rs2,
  output [6:0] func_7
);


  assign func_3 = _32_bit_instructions[14:12];
  assign func_7 = _32_bit_instructions[31:25];
  assign opcode = _32_bit_instructions[6:0];
  assign rd = _32_bit_instructions[11:7];
  assign rs1 = _32_bit_instructions[19:15];
  assign rs2 = _32_bit_instructions[24:20];
endmodule

module Control_Unit (
  input  [6:0] in_1,
  input  [2:0] in_2,
  input  [1:0] in_3,
  output [5:0] alu_op,
  output OPERAND_B,
  output regWrite,
  output OPERAND_A,
  output BRANCH,
  output MEM_TO_REG,
  output MEM_WRIITE
);

  wire and_1_out, and_2_out, and_3_out, and_4_out, and_5_out, and_6_out, comparator_1_eq, comparator_2_eq,
       comparator_3_eq, comparator_4_eq, comparator_5_eq, comparator_6_eq, comparator_7_eq, comparator_8_eq,
       comparator_9_eq, comparator_10_eq, comparator_11_eq, comparator_12_eq, comparator_13_eq,
       comparator_14_eq, comparator_15_eq, comparator_16_eq, comparator_17_eq, comparator_18_eq,
       comparator_19_eq, comparator_20_eq, comparator_21_eq, comparator_22_eq, comparator_23_eq,
       comparator_24_eq, comparator_25_eq, comparator_26_eq, comparator_27_eq, comparator_28_eq,
       comparator_29_eq, comparator_30_eq, comparator_31_eq, comparator_32_eq, comparator_33_eq,
       comparator_34_eq, comparator_35_eq, comparator_36_eq, comparator_37_eq, comparator_38_eq,
       comparator_39_eq, comparator_40_eq, comparator_41_eq, comparator_42_eq, comparator_43_eq,
       comparator_44_eq, comparator_45_eq, comparator_46_eq, comparator_47_eq, comparator_48_eq,
       comparator_49_eq, comparator_50_eq, comparator_51_eq, comparator_52_eq, comparator_53_eq,
       comparator_54_eq, comparator_55_eq, comparator_56_eq, comparator_57_eq, demultiplexer_1_out0,
       demultiplexer_1_out1, demultiplexer_1_out2, demultiplexer_1_out3, demultiplexer_1_out4,
       demultiplexer_1_out5, demultiplexer_1_out7, demultiplexer_1_out8, demultiplexer_2_out0,
       demultiplexer_2_out1, demultiplexer_2_out2, demultiplexer_2_out3, demultiplexer_2_out4,
       demultiplexer_2_out5, demultiplexer_2_out6, demultiplexer_2_out7, demultiplexer_2_out8,
       demultiplexer_3_out0, demultiplexer_3_out1, demultiplexer_3_out4, demultiplexer_3_out5,
       demultiplexer_3_out6, demultiplexer_3_out7, demultiplexer_4_out0, demultiplexer_4_out1,
       demultiplexer_4_out2, demultiplexer_4_out3, demultiplexer_4_out4, demultiplexer_5_out0,
       demultiplexer_5_out1, demultiplexer_5_out2, demultiplexer_6_out0, demultiplexer_6_out1,
       demultiplexer_7_out0, demultiplexer_7_out1, demultiplexer_8_out0, demultiplexer_8_out1, not_1_out,
       not_2_out, not_3_out, not_4_out, not_5_out, not_6_out, or_1_out, or_2_out, or_3_out, or_5_out,
       or_6_out, or_7_out, or_8_out, or_9_out, or_10_out;
  wire [2:0] bge;
  wire [4:0] add, multiplexer_1_out;

  Demultiplexer #(.select(4), .enable("false")) demultiplexer_1 (
    .out0(demultiplexer_1_out0), .out1(demultiplexer_1_out1), .out2(demultiplexer_1_out2),
    .out3(demultiplexer_1_out3), .out4(demultiplexer_1_out4), .out5(demultiplexer_1_out5),
    .out6(demultiplexer_1_out5), .out7(demultiplexer_1_out7), .out8(demultiplexer_1_out8),
    .in(comparator_1_eq), .sel({1'b0, in_2}));  // open: out9, out10, out11, out12, out13, out14, out15
  Comparator #(.width(7)) comparator_1 (.a(7'b0010011), .b(in_1), .eq(comparator_1_eq));  // open: gt, lt
  Demultiplexer #(.select(4), .enable("false")) demultiplexer_2 (
    .out0(demultiplexer_2_out0), .out1(demultiplexer_2_out1), .out2(demultiplexer_2_out2),
    .out3(demultiplexer_2_out3), .out4(demultiplexer_2_out4), .out5(demultiplexer_2_out5),
    .out6(demultiplexer_2_out6), .out7(demultiplexer_2_out7), .out8(demultiplexer_2_out8),
    .in(comparator_2_eq), .sel({1'b0, in_2}));  // open: out9, out10, out11, out12, out13, out14, out15
  Comparator #(.width(7)) comparator_2 (.a(7'b0110011), .b(in_1), .eq(comparator_2_eq));  // open: gt, lt
  Demultiplexer #(.select(3), .enable("false")) demultiplexer_3 (
    .out0(demultiplexer_3_out0), .out1(demultiplexer_3_out1), .out4(demultiplexer_3_out4),
    .out5(demultiplexer_3_out5), .out6(demultiplexer_3_out6), .out7(demultiplexer_3_out7),
    .in(comparator_3_eq), .sel(in_2));  // open: out2, out3
  Comparator #(.width(7)) comparator_3 (.a(7'b1100011), .b(in_1), .eq(comparator_3_eq));  // open: gt, lt
  Comparator #(.width(7)) comparator_4 (.a(7'b0000011), .b(in_1), .eq(comparator_4_eq));  // open: gt, lt
  Demultiplexer #(.select(3), .enable("false")) demultiplexer_4 (
    .out0(demultiplexer_4_out0), .out1(demultiplexer_4_out1), .out2(demultiplexer_4_out2),
    .out3(demultiplexer_4_out3), .out4(demultiplexer_4_out4), .in(comparator_4_eq), .sel(in_2));  // open: out5, out6, out7
  Demultiplexer #(.select(2), .enable("false")) demultiplexer_5 (
    .out0(demultiplexer_5_out0), .out1(demultiplexer_5_out1), .out2(demultiplexer_5_out2),
    .in(comparator_5_eq), .sel(in_2[1:0]));  // open: out3
  Comparator #(.width(7)) comparator_5 (.a(7'b0100011), .b(in_1), .eq(comparator_5_eq));  // open: gt, lt
  Comparator #(.width(7)) comparator_6 (.a(7'b1100111), .b(in_1), .eq(comparator_6_eq));  // open: gt, lt
  Comparator #(.width(7)) comparator_7 (.a(7'b1101111), .b(in_1), .eq(comparator_7_eq));  // open: gt, lt
  Comparator #(.width(7)) comparator_8 (.a(7'b0010111), .b(in_1), .eq(comparator_8_eq));  // open: gt, lt
  Comparator #(.width(7)) comparator_9 (.a(7'b0110111), .b(in_1), .eq(comparator_9_eq));  // open: gt, lt
  // Probe on 5'b00100
  // Probe on 5'b11100
  Comparator #(.width(7)) comparator_10 (.a(7'b0000011), .b(in_1), .eq(comparator_10_eq));  // open: gt, lt
  Comparator #(.width(7)) comparator_11 (.a(7'b0010011), .b(in_1), .eq(comparator_11_eq));  // open: gt, lt
  Comparator #(.width(7)) comparator_12 (.a({7{1'b1}}), .b(in_1), .eq(comparator_12_eq));  // open: gt, lt
  Comparator #(.width(7)) comparator_13 (.a(7'b0100011), .b(in_1), .eq(comparator_13_eq));  // open: gt, lt
  Comparator #(.width(7)) comparator_14 (.a(7'b0110011), .b(in_1), .eq(comparator_14_eq));  // open: gt, lt
  Comparator #(.width(7)) comparator_15 (.a(7'b1101111), .b(in_1), .eq(comparator_15_eq));  // open: gt, lt
  Comparator #(.width(7)) comparator_16 (.a(7'b0110111), .b(in_1), .eq(comparator_16_eq));  // open: gt, lt
  Comparator #(.width(7)) comparator_17 (.a(7'b1100011), .b(in_1), .eq(comparator_17_eq));  // open: gt, lt
  or or_1 (or_1_out, demultiplexer_2_out5, demultiplexer_2_out6);
  assign bge = comparator_6_eq ? 3'b011 : 3'bz;  // Controlled_Buffer controlled_buffer_1
  LED led_1 (.in(comparator_6_eq));
  assign bge = comparator_7_eq ? 3'b100 : 3'bz;  // Controlled_Buffer controlled_buffer_2
  LED led_2 (.in(comparator_7_eq));
  assign add = comparator_8_eq ? 5'b01110 : 5'bz;  // Controlled_Buffer controlled_buffer_3
  LED led_3 (.in(comparator_8_eq));
  assign add = comparator_9_eq ? 5'b11100 : 5'bz;  // Controlled_Buffer controlled_buffer_4
  LED led_4 (.in(comparator_9_eq));
  Comparator #(.width(7)) comparator_18 (.a(7'b0000011), .b(in_1), .eq(comparator_18_eq));  // open: gt, lt
  Comparator #(.width(7)) comparator_19 (.a(7'b0010011), .b(in_1), .eq(comparator_19_eq));  // open: gt, lt
  Comparator #(.width(7)) comparator_20 (.a({7{1'b1}}), .b(in_1), .eq(comparator_20_eq));  // open: gt, lt
  Comparator #(.width(7)) comparator_21 (.a(7'b0100011), .b(in_1), .eq(comparator_21_eq));  // open: gt, lt
  Comparator #(.width(7)) comparator_22 (.a(7'b1100011), .b(in_1), .eq(comparator_22_eq));  // open: gt, lt
  Comparator #(.width(7)) comparator_23 (.a(7'b0110011), .b(in_1), .eq(comparator_23_eq));  // open: gt, lt
  Comparator #(.width(7)) comparator_24 (.a(7'b1101111), .b(in_1), .eq(comparator_24_eq));  // open: gt, lt
  Comparator #(.width(7)) comparator_25 (.a(7'b0110111), .b(in_1), .eq(comparator_25_eq));  // open: gt, lt
  assign add = demultiplexer_4_out4 ? 5'b00100 : 5'bz;  // Controlled_Buffer controlled_buffer_5
  LED led_5 (.in(demultiplexer_4_out4));
  assign add = demultiplexer_5_out2 ? 5'b10001 : 5'bz;  // Controlled_Buffer controlled_buffer_6
  or or_2 (or_2_out, comparator_18_eq, comparator_19_eq, comparator_20_eq);
  assign add = demultiplexer_4_out3 ? 5'b00011 : 5'bz;  // Controlled_Buffer controlled_buffer_7
  assign add = demultiplexer_4_out2 ? 5'b00010 : 5'bz;  // Controlled_Buffer controlled_buffer_8
  assign add = demultiplexer_5_out1 ? 5'b10000 : 5'bz;  // Controlled_Buffer controlled_buffer_9
  assign add = demultiplexer_5_out0 ? 5'b01111 : 5'bz;  // Controlled_Buffer controlled_buffer_10
  LED led_6 (.in(demultiplexer_5_out1));
  LED led_7 (.in(demultiplexer_5_out2));
  and and_1 (and_1_out, comparator_21_eq, 1'b0);
  and and_2 (and_2_out, comparator_22_eq, 1'b0);
  and and_3 (and_3_out, comparator_23_eq, 1'b1);
  and and_4 (and_4_out, comparator_24_eq, 1'b1);
  and and_5 (and_5_out, comparator_25_eq, 1'b1);
  assign add = demultiplexer_4_out1 ? 5'b00001 : 5'bz;  // Controlled_Buffer controlled_buffer_11
  LED led_8 (.in(demultiplexer_4_out2));
  LED led_9 (.in(demultiplexer_4_out3));
  LED led_10 (.in(demultiplexer_5_out0));
  and and_6 (and_6_out, or_2_out, 1'b1);
  not not_1 (not_1_out, or_3_out);
  or or_3 (or_3_out, comparator_10_eq, comparator_11_eq, comparator_12_eq, comparator_13_eq, comparator_14_eq, comparator_15_eq, comparator_16_eq);
  assign add = demultiplexer_4_out0 ? {5{1'b0}} : 5'bz;  // Controlled_Buffer controlled_buffer_12
  LED led_11 (.in(demultiplexer_4_out0));
  LED led_12 (.in(demultiplexer_4_out1));
  assign bge = demultiplexer_3_out7 ? 3'b010 : 3'bz;  // Controlled_Buffer controlled_buffer_13
  or or_4 (regWrite, and_6_out, and_1_out, and_2_out, and_3_out, and_4_out, and_5_out);
  and and_7 (BRANCH, not_1_out, comparator_17_eq);
  LED led_13 (.in(demultiplexer_1_out7));
  LED led_14 (.in(demultiplexer_1_out8));
  // Probe on 3'b010
  or or_5 (or_5_out, demultiplexer_3_out7, comparator_6_eq, comparator_7_eq, demultiplexer_3_out5, demultiplexer_3_out6);
  assign bge = demultiplexer_3_out6 ? 3'b001 : 3'bz;  // Controlled_Buffer controlled_buffer_14
  assign bge = not_2_out ? 3'b101 : 3'bz;  // Controlled_Buffer controlled_buffer_15
  not not_2 (not_2_out, or_5_out);
  assign add = demultiplexer_1_out8 ? 5'b01101 : 5'bz;  // Controlled_Buffer controlled_buffer_16
  assign add = demultiplexer_1_out7 ? 5'b01100 : 5'bz;  // Controlled_Buffer controlled_buffer_17
  Demultiplexer #(.select(2), .enable("false")) demultiplexer_6 (
    .out0(demultiplexer_6_out0), .out1(demultiplexer_6_out1), .in(demultiplexer_1_out5), .sel(in_3));  // open: out2, out3
  assign bge = demultiplexer_3_out5 ? 3'b000 : 3'bz;  // Controlled_Buffer controlled_buffer_18
  assign add = demultiplexer_3_out4 ? {5{1'b1}} : 5'bz;  // Controlled_Buffer controlled_buffer_19
  LED led_15 (.in(demultiplexer_3_out7));
  assign add = demultiplexer_6_out1 ? 5'b01011 : 5'bz;  // Controlled_Buffer controlled_buffer_20
  assign add = demultiplexer_3_out1 ? 5'b11110 : 5'bz;  // Controlled_Buffer controlled_buffer_21
  LED led_16 (.in(demultiplexer_3_out5));
  LED led_17 (.in(demultiplexer_3_out6));
  assign add = demultiplexer_6_out0 ? 5'b01010 : 5'bz;  // Controlled_Buffer controlled_buffer_22
  assign add = demultiplexer_1_out4 ? 5'b01001 : 5'bz;  // Controlled_Buffer controlled_buffer_23
  LED led_18 (.in(demultiplexer_6_out0));
  LED led_19 (.in(demultiplexer_6_out1));
  assign add = demultiplexer_3_out0 ? 5'b11101 : 5'bz;  // Controlled_Buffer controlled_buffer_24
  LED led_20 (.in(demultiplexer_3_out0));
  LED led_21 (.in(demultiplexer_3_out1));
  LED led_22 (.in(demultiplexer_3_out4));
  assign add = demultiplexer_1_out3 ? 5'b01000 : 5'bz;  // Controlled_Buffer controlled_buffer_25
  assign add = demultiplexer_2_out8 ? 5'b11011 : 5'bz;  // Controlled_Buffer controlled_buffer_26
  LED led_23 (.in(demultiplexer_2_out8));
  assign add = demultiplexer_1_out2 ? 5'b00111 : 5'bz;  // Controlled_Buffer controlled_buffer_27
  assign add = demultiplexer_1_out1 ? 5'b00110 : 5'bz;  // Controlled_Buffer controlled_buffer_28
  assign add = demultiplexer_2_out7 ? 5'b11010 : 5'bz;  // Controlled_Buffer controlled_buffer_29
  LED led_24 (.in(demultiplexer_2_out7));
  Demultiplexer #(.select(2), .enable("false")) demultiplexer_7 (
    .out0(demultiplexer_7_out0), .out1(demultiplexer_7_out1), .in(or_1_out), .sel(in_3));  // open: out2, out3
  assign add = demultiplexer_1_out0 ? 5'b00101 : 5'bz;  // Controlled_Buffer controlled_buffer_30
  LED led_25 (.in(demultiplexer_1_out3));
  LED led_26 (.in(demultiplexer_1_out4));
  assign add = demultiplexer_7_out1 ? 5'b11001 : 5'bz;  // Controlled_Buffer controlled_buffer_31
  LED led_27 (.in(demultiplexer_7_out1));
  LED led_28 (.in(demultiplexer_1_out1));
  LED led_29 (.in(demultiplexer_1_out2));
  assign add = demultiplexer_7_out0 ? 5'b11000 : 5'bz;  // Controlled_Buffer controlled_buffer_32
  LED led_30 (.in(demultiplexer_7_out0));
  Comparator #(.width(7)) comparator_26 (.a(7'b0000011), .b(in_1), .eq(comparator_26_eq));  // open: gt, lt
  Comparator #(.width(7)) comparator_27 (.a(7'b0010011), .b(in_1), .eq(comparator_27_eq));  // open: gt, lt
  Comparator #(.width(7)) comparator_28 (.a({7{1'b1}}), .b(in_1), .eq(comparator_28_eq));  // open: gt, lt
  Comparator #(.width(7)) comparator_29 (.a(7'b0100011), .b(in_1), .eq(comparator_29_eq));  // open: gt, lt
  Comparator #(.width(7)) comparator_30 (.a(7'b1100011), .b(in_1), .eq(comparator_30_eq));  // open: gt, lt
  Comparator #(.width(7)) comparator_31 (.a(7'b1101111), .b(in_1), .eq(comparator_31_eq));  // open: gt, lt
  Comparator #(.width(7)) comparator_32 (.a(7'b0110111), .b(in_1), .eq(comparator_32_eq));  // open: gt, lt
  Comparator #(.width(7)) comparator_33 (.a(7'b0110011), .b(in_1), .eq(comparator_33_eq));  // open: gt, lt
  Comparator #(.width(7)) comparator_34 (.a(7'b0000011), .b(in_1), .eq(comparator_34_eq));  // open: gt, lt
  Comparator #(.width(7)) comparator_35 (.a(7'b0010011), .b(in_1), .eq(comparator_35_eq));  // open: gt, lt
  Comparator #(.width(7)) comparator_36 (.a({7{1'b1}}), .b(in_1), .eq(comparator_36_eq));  // open: gt, lt
  Comparator #(.width(7)) comparator_37 (.a(7'b0100011), .b(in_1), .eq(comparator_37_eq));  // open: gt, lt
  Comparator #(.width(7)) comparator_38 (.a(7'b0110011), .b(in_1), .eq(comparator_38_eq));  // open: gt, lt
  Comparator #(.width(7)) comparator_39 (.a(7'b1101111), .b(in_1), .eq(comparator_39_eq));  // open: gt, lt
  Comparator #(.width(7)) comparator_40 (.a(7'b0110111), .b(in_1), .eq(comparator_40_eq));  // open: gt, lt
  Comparator #(.width(7)) comparator_41 (.a(7'b1100011), .b(in_1), .eq(comparator_41_eq));  // open: gt, lt
  LED led_31 (.in(demultiplexer_1_out0));
  or or_6 (or_6_out, comparator_26_eq, comparator_27_eq, comparator_28_eq, comparator_29_eq, comparator_30_eq, comparator_31_eq, comparator_32_eq);
  not not_3 (not_3_out, comparator_33_eq);
  assign add = demultiplexer_2_out4 ? 5'b10111 : 5'bz;  // Controlled_Buffer controlled_buffer_33
  assign add = demultiplexer_2_out3 ? 5'b10110 : 5'bz;  // Controlled_Buffer controlled_buffer_34
  LED led_32 (.in(demultiplexer_2_out4));
  not not_4 (not_4_out, or_7_out);
  or or_7 (or_7_out, comparator_35_eq, comparator_36_eq, comparator_37_eq, comparator_38_eq, comparator_39_eq, comparator_40_eq, comparator_41_eq);
  assign add = demultiplexer_2_out2 ? 5'b10101 : 5'bz;  // Controlled_Buffer controlled_buffer_35
  assign add = demultiplexer_2_out1 ? 5'b10100 : 5'bz;  // Controlled_Buffer controlled_buffer_36
  LED led_33 (.in(demultiplexer_2_out2));
  LED led_34 (.in(demultiplexer_2_out3));
  and and_8 (OPERAND_A, or_6_out, not_3_out);
  and and_9 (MEM_TO_REG, comparator_34_eq, not_4_out);
  Demultiplexer #(.select(2), .enable("false")) demultiplexer_8 (
    .out0(demultiplexer_8_out0), .out1(demultiplexer_8_out1), .in(demultiplexer_2_out0), .sel(in_3));  // open: out2, out3
  LED led_35 (.in(demultiplexer_2_out1));
  assign add = demultiplexer_8_out0 ? 5'b10010 : 5'bz;  // Controlled_Buffer controlled_buffer_37
  assign add = demultiplexer_8_out1 ? 5'b10011 : 5'bz;  // Controlled_Buffer controlled_buffer_38
  LED led_36 (.in(demultiplexer_8_out0));
  LED led_37 (.in(demultiplexer_8_out1));
  Multiplexer #(.select(5), .width(5), .enable("false")) multiplexer_1 (
    .in0({5{1'b0}}), .in1(5'b00001), .in2(5'b00010), .in3(5'b00011), .in4(5'b00100), .in5(5'b00101),
    .in6(5'b00110), .in7(5'b00111), .in8(5'b01000), .in9(5'b01001), .in10(5'b01010), .in11(5'b01011),
    .in12(5'b01100), .in13(5'b01101), .in14(5'b01110), .in15(5'b01111), .in16(5'b10000), .in17(5'b10001),
    .in18(5'b10010), .in19(5'b10011), .in20(5'b10100), .in21(5'b10101), .in22(5'b10110), .in23(5'b10111),
    .in24(5'b11000), .in25(5'b11001), .in26(5'b11010), .in27(5'b11011), .in28(5'b11100), .in29(5'b11101),
    .in30(5'b11110), .in31({5{1'b1}}), .out(multiplexer_1_out), .sel(add));
  Comparator #(.width(7)) comparator_42 (.a(7'b0000011), .b(in_1), .eq(comparator_42_eq));  // open: gt, lt
  Comparator #(.width(7)) comparator_43 (.a(7'b0010011), .b(in_1), .eq(comparator_43_eq));  // open: gt, lt
  Comparator #(.width(7)) comparator_44 (.a({7{1'b1}}), .b(in_1), .eq(comparator_44_eq));  // open: gt, lt
  Comparator #(.width(7)) comparator_45 (.a(7'b0100011), .b(in_1), .eq(comparator_45_eq));  // open: gt, lt
  Comparator #(.width(7)) comparator_46 (.a(7'b0110111), .b(in_1), .eq(comparator_46_eq));  // open: gt, lt
  Comparator #(.width(7)) comparator_47 (.a(7'b0110011), .b(in_1), .eq(comparator_47_eq));  // open: gt, lt
  Comparator #(.width(7)) comparator_48 (.a(7'b1100011), .b(in_1), .eq(comparator_48_eq));  // open: gt, lt
  Comparator #(.width(7)) comparator_49 (.a(7'b1101111), .b(in_1), .eq(comparator_49_eq));  // open: gt, lt
  // Probe on multiplexer_1_out
  or or_8 (or_8_out, comparator_48_eq, comparator_49_eq);
  Comparator #(.width(7)) comparator_50 (.a(7'b0100011), .b(in_1), .eq(comparator_50_eq));  // open: gt, lt
  Comparator #(.width(7)) comparator_51 (.a(7'b0010011), .b(in_1), .eq(comparator_51_eq));  // open: gt, lt
  Comparator #(.width(7)) comparator_52 (.a({7{1'b1}}), .b(in_1), .eq(comparator_52_eq));  // open: gt, lt
  Comparator #(.width(7)) comparator_53 (.a(7'b0000011), .b(in_1), .eq(comparator_53_eq));  // open: gt, lt
  Comparator #(.width(7)) comparator_54 (.a(7'b0110011), .b(in_1), .eq(comparator_54_eq));  // open: gt, lt
  Comparator #(.width(7)) comparator_55 (.a(7'b1101111), .b(in_1), .eq(comparator_55_eq));  // open: gt, lt
  Comparator #(.width(7)) comparator_56 (.a(7'b0110111), .b(in_1), .eq(comparator_56_eq));  // open: gt, lt
  Comparator #(.width(7)) comparator_57 (.a(7'b1100011), .b(in_1), .eq(comparator_57_eq));  // open: gt, lt
  // Probe on alu_op
  Multiplexer #(.select(3), .width(6), .enable("false")) multiplexer_2 (
    .in0(6'b100000), .in1(6'b100001), .in2(6'b100010), .in3(6'b100011), .in4(6'b100100),
    .in5({1'b0, multiplexer_1_out}), .out(alu_op), .sel(bge));  // open: in6, in7
  not not_5 (not_5_out, or_9_out);
  or or_9 (or_9_out, comparator_42_eq, comparator_43_eq, comparator_44_eq, comparator_45_eq, comparator_46_eq, comparator_47_eq);
  or or_10 (or_10_out, comparator_51_eq, comparator_52_eq, comparator_53_eq, comparator_54_eq, comparator_55_eq, comparator_56_eq, comparator_57_eq);
  not not_6 (not_6_out, or_10_out);
  and and_10 (OPERAND_B, not_5_out, or_8_out);
  and and_11 (MEM_WRIITE, comparator_50_eq, not_6_out);

  // Other names for the same wires on the sheet: _14_12_FUNC_3[2:0] = in_2; addi[4:0] = add; and[4:0] = add;
  //   andi[4:0] = add; auipc[4:0] = add; beq[4:0] = add; blt[4:0] = add; bne[4:0] = add; lb[4:0] = add;
  //   lbu[4:0] = add; lh[4:0] = add; lhu[4:0] = add; lui[4:0] = add; lw[4:0] = add; or[4:0] = add; ori[4:0] = add;
  //   sb[4:0] = add; sh[4:0] = add; sll[4:0] = add; slli[4:0] = add; slt[4:0] = add; slti[4:0] = add;
  //   sltiu[4:0] = add; sltu[4:0] = add; sra[4:0] = add; srai[4:0] = add; srl[4:0] = add; srli[4:0] = add;
  //   sub[4:0] = add; sw[4:0] = add; xor[4:0] = add; xori[4:0] = add; bgeu[2:0] = bge; bltu[2:0] = bge; en[2:0] = bge;
  //   jal[2:0] = bge; jalr[2:0] = bge; _30_31_FUNC_7[1:0] = in_3; Opcode[6:0] = in_1

  // Notes on the sheet:
  //   alu i-type
  //   r-type
  //   sb-type
  //   load i-type
  //   s-type
  //   I-TYPE
  //   S-TYPE
  //   SB-TYPE
  //   R-TYPE
  //   UJ-TYPE
  //   U-TYPE
  //   JALR i-type
  //   JAL uj-type
  //   AUIPC u-type
  //   LUI u-type
  //   load i-type
  //   alu i-type
  //   jalr i-type
  //   store
  //   SB-type
  //   r-type
  //   jal UJ-type
  //   auipc/lui U-type
  //   load i-type
  //   alu i-type
  //   jalr i-type
  //   store
  //   r-type
  //   jal UJ-type
  //   auipc/lui U-type
  //   SB-type
  //   WRITE REG
  //   BRANCH
  //   load i-type
  //   alu i-type
  //   jalr i-type
  //   store
  //   SB-type
  //   jal UJ-type
  //   auipc/lui U-type
  //   r-type
  //   load i-type
  //   alu i-type
  //   jalr i-type
  //   store
  //   r-type
  //   jal UJ-type
  //   auipc/lui U-type
  //   SB-type
  //   OPERAND A
  //   MEM TO REG
  //   ALL 37 OPERATIONS
  //   load i-type
  //   alu i-type
  //   jalr i-type
  //   store
  //   auipc/lui U-type
  //   r-type
  //   SB-type
  //   jal UJ-type
  //   store
  //   alu i-type
  //   jalr i-type
  //   load i-type
  //   r-type
  //   jal UJ-type
  //   auipc/lui U-type
  //   SB-type
  //   OPERAND B
  //   MEM WRITE
endmodule

// sw
module Control_Decoder (
  input  [31:0] _32bit_instruction,
  output regWrite,
  output [4:0] rd,
  output mem_to_reg,
  output mem_write,
  output [4:0] rs1,
  output operand_a,
  output [4:0] rs2,
  output operand_b,
  output branch,
  output [5:0] aluOP,
  output [31:0] _32bit_immediate
);

  wire [2:0] decoder_1_func_3;
  wire [6:0] decoder_1_func_7, decoder_1_opcode;

  decoder decoder_1 (
    ._32_bit_instructions(_32bit_instruction), .opcode(decoder_1_opcode), .rd(rd), .func_3(decoder_1_func_3),
    .rs1(rs1), .rs2(rs2), .func_7(decoder_1_func_7));
  // Probe on decoder_1_opcode
  immediate_generation immediate_generation_1 (
    .in_1(decoder_1_opcode), .in_2(_32bit_instruction), .out_3(_32bit_immediate));
  // Control_Unit control_unit_1: pin names not known; wires that end beside it: decoder_1_opcode, decoder_1_func_3, decoder_1_func_7[6:5], regWrite, mem_to_reg, aluOP, mem_write, operand_a, operand_b, branch
endmodule

module immediate_generation (
  input  [6:0] in_1,
  input  [31:0] in_2,
  output [31:0] out_3
);

  wire comparator_1_eq, comparator_2_eq, comparator_3_eq, comparator_4_eq, comparator_5_eq, comparator_6_eq,
       comparator_7_eq, or_1_out;
  wire [2:0] controlled_buffer_6_out;
  wire [11:0] controlled_buffer_1_out, controlled_buffer_3_out;
  wire [12:0] controlled_buffer_4_out;
  wire [20:0] controlled_buffer_2_out;
  wire [31:0] bit_extender_1_out, bit_extender_2_out, bit_extender_3_out, bit_extender_4_out,
       controlled_buffer_5_out;

  Comparator #(.width(7)) comparator_1 (.a(7'b0000011), .b(in_1), .eq(comparator_1_eq));  // open: gt, lt
  Comparator #(.width(7)) comparator_2 (.a(7'b0010011), .b(in_1), .eq(comparator_2_eq));  // open: gt, lt
  Comparator #(.width(7)) comparator_3 (.a({7{1'b1}}), .b(in_1), .eq(comparator_3_eq));  // open: gt, lt
  Comparator #(.width(7)) comparator_4 (.a(7'b0100011), .b(in_1), .eq(comparator_4_eq));  // open: gt, lt
  Comparator #(.width(7)) comparator_5 (.a(7'b1100011), .b(in_1), .eq(comparator_5_eq));  // open: gt, lt
  Comparator #(.width(7)) comparator_6 (.a(7'b1101111), .b(in_1), .eq(comparator_6_eq));  // open: gt, lt
  Comparator #(.width(7)) comparator_7 (.a(7'b0110111), .b(in_1), .eq(comparator_7_eq));  // open: gt, lt
  or or_1 (or_1_out, comparator_1_eq, comparator_2_eq, comparator_3_eq);
  // Probe on {in_2[31:25], in_2[11:7]}
  assign controlled_buffer_1_out = or_1_out ? in_2[31:20] : 12'bz;  // Controlled_Buffer controlled_buffer_1
  assign controlled_buffer_2_out = comparator_7_eq ? {in_2[31], in_2[19:12], in_2[20], in_2[30:21], 1'b0} : 21'bz;  // Controlled_Buffer controlled_buffer_2
  // Probe on controlled_buffer_1_out
  assign controlled_buffer_3_out = comparator_4_eq ? {in_2[31:25], in_2[11:7]} : 12'bz;  // Controlled_Buffer controlled_buffer_3
  // Probe on controlled_buffer_4_out
  assign controlled_buffer_4_out = comparator_5_eq ? {in_2[31], in_2[7], in_2[30:25], in_2[11:8], 1'b0} : 13'bz;  // Controlled_Buffer controlled_buffer_4
  // Probe on {in_2[31:12], {12{1'b0}}}
  assign controlled_buffer_5_out = comparator_6_eq ? {in_2[31:12], {12{1'b0}}} : 32'bz;  // Controlled_Buffer controlled_buffer_5
  assign controlled_buffer_6_out = or_1_out ? 3'b000 : 3'bz;  // Controlled_Buffer controlled_buffer_6
  assign bit_extender_1_out = {{20{controlled_buffer_1_out[11]}}, controlled_buffer_1_out};  // Bit_Extender bit_extender_1
  // Probe on bit_extender_2_out
  assign bit_extender_2_out = {{20{controlled_buffer_3_out[11]}}, controlled_buffer_3_out};  // Bit_Extender bit_extender_2
  assign controlled_buffer_6_out = comparator_4_eq ? 3'b001 : 3'bz;  // Controlled_Buffer controlled_buffer_7
  assign bit_extender_3_out = {{19{controlled_buffer_4_out[12]}}, controlled_buffer_4_out};  // Bit_Extender bit_extender_3
  assign controlled_buffer_6_out = comparator_5_eq ? 3'b010 : 3'bz;  // Controlled_Buffer controlled_buffer_8
  assign controlled_buffer_6_out = comparator_6_eq ? 3'b011 : 3'bz;  // Controlled_Buffer controlled_buffer_9
  assign bit_extender_4_out = {{11{controlled_buffer_2_out[20]}}, controlled_buffer_2_out};  // Bit_Extender bit_extender_4
  assign controlled_buffer_6_out = comparator_7_eq ? 3'b100 : 3'bz;  // Controlled_Buffer controlled_buffer_10
  Multiplexer #(.select(3), .width(32), .enable("false")) multiplexer_1 (
    .in0(bit_extender_1_out), .in1(bit_extender_2_out), .in2(bit_extender_3_out),
    .in3(controlled_buffer_5_out), .in4(bit_extender_4_out), .out(out_3), .sel(controlled_buffer_6_out));  // open: in5, in6, in7

  // Notes on the sheet:
  //   load i-type
  //   alu i-type
  //   jalr i-type
  //   store
  //   SB-type
  //   jal UJ-type
  //   auipc/lui U-type
endmodule

module _32_bit_reg_reg_file (
  input  [31:0] write_data,
  input  writeReg,
  input  [4:0] destination_register,
  input  [4:0] read_register_1,
  input  [4:0] read_register_2,
  input  clock,
  input  reset,
  output [31:0] read_data_1,
  output [31:0] read_data_2
);

  wire d1, d2, d3, d4, d5, d6, d7, d8, d9, d10, d11, d12, d13, d14, d15, d16, d17, d18, d19, d20, d21, d22,
       d23, d24, d25, d26, d27, d28, d29, d30, d31, d32;
  wire [31:0] s1, s2, s3, s4, s5, s6, s7, s8, s9, s10, s11, s12, s13, s14, s15, s16, s17, s18, s19, s20, s21,
       s22, s23, s24, s25, s26, s27, s28, s29, s30, s31, s32;

  Demultiplexer #(.select(5), .enable("false")) demultiplexer_1 (
    .out0(d1), .out1(d2), .out2(d3), .out3(d4), .out4(d5), .out5(d6), .out6(d7), .out7(d8), .out8(d9),
    .out9(d10), .out10(d11), .out11(d12), .out12(d13), .out13(d14), .out14(d15), .out15(d16), .out16(d17),
    .out17(d18), .out18(d19), .out19(d20), .out20(d21), .out21(d22), .out22(d23), .out23(d24), .out24(d25),
    .out25(d26), .out26(d27), .out27(d28), .out28(d29), .out29(d30), .out30(d31), .out31(d32), .in(writeReg),
    .sel(destination_register));
  Register #(.width(32)) register_1 (.D(write_data), .en(d1), .Q(s1), .clk(clock), .clr(reset));
  Register #(.width(32)) register_2 (.D(write_data), .en(d2), .Q(s2), .clk(clock), .clr(reset));
  Register #(.width(32)) register_3 (.D(write_data), .en(d3), .Q(s3), .clk(clock), .clr(reset));
  Register #(.width(32)) register_4 (.D(write_data), .en(d4), .Q(s4), .clk(clock), .clr(reset));
  Register #(.width(32)) register_5 (.D(write_data), .en(d5), .Q(s5), .clk(clock), .clr(reset));
  Register #(.width(32)) register_6 (.D(write_data), .en(d6), .Q(s6), .clk(clock), .clr(reset));
  Register #(.width(32)) register_7 (.D(write_data), .en(d13), .Q(s13), .clk(clock), .clr(reset));
  Register #(.width(32)) register_8 (.D(write_data), .en(d7), .Q(s7), .clk(clock), .clr(reset));
  Register #(.width(32)) register_9 (.D(write_data), .en(d8), .Q(s8), .clk(clock), .clr(reset));
  Register #(.width(32)) register_10 (.D(write_data), .en(d9), .Q(s9), .clk(clock), .clr(reset));
  Register #(.width(32)) register_11 (.D(write_data), .en(d10), .Q(s10), .clk(clock), .clr(reset));
  Register #(.width(32)) register_12 (.D(write_data), .en(d11), .Q(s11), .clk(clock), .clr(reset));
  Register #(.width(32)) register_13 (.D(write_data), .en(d12), .Q(s12), .clk(clock), .clr(reset));
  Register #(.width(32)) register_14 (.D(write_data), .en(d32), .Q(s32), .clk(clock), .clr(reset));
  Register #(.width(32)) register_15 (.D(write_data), .en(d14), .Q(s14), .clk(clock), .clr(reset));
  Register #(.width(32)) register_16 (.D(write_data), .en(d15), .Q(s15), .clk(clock), .clr(reset));
  Register #(.width(32)) register_17 (.D(write_data), .en(d16), .Q(s16), .clk(clock), .clr(reset));
  Register #(.width(32)) register_18 (.D(write_data), .en(d17), .Q(s17), .clk(clock), .clr(reset));
  Register #(.width(32)) register_19 (.D(write_data), .en(d18), .Q(s18), .clk(clock), .clr(reset));
  Register #(.width(32)) register_20 (.D(write_data), .en(d19), .Q(s19), .clk(clock), .clr(reset));
  Register #(.width(32)) register_21 (.D(write_data), .en(d20), .Q(s20), .clk(clock), .clr(reset));
  Register #(.width(32)) register_22 (.D(write_data), .en(d21), .Q(s21), .clk(clock), .clr(reset));
  Register #(.width(32)) register_23 (.D(write_data), .en(d22), .Q(s22), .clk(clock), .clr(reset));
  Register #(.width(32)) register_24 (.D(write_data), .en(d23), .Q(s23), .clk(clock), .clr(reset));
  Register #(.width(32)) register_25 (.D(write_data), .en(d24), .Q(s24), .clk(clock), .clr(reset));
  Register #(.width(32)) register_26 (.D(write_data), .en(d25), .Q(s25), .clk(clock), .clr(reset));
  Register #(.width(32)) register_27 (.D(write_data), .en(d26), .Q(s26), .clk(clock), .clr(reset));
  Register #(.width(32)) register_28 (.D(write_data), .en(d27), .Q(s27), .clk(clock), .clr(reset));
  Register #(.width(32)) register_29 (.D(write_data), .en(d28), .Q(s28), .clk(clock), .clr(reset));
  Register #(.width(32)) register_30 (.D(write_data), .en(d29), .Q(s29), .clk(clock), .clr(reset));
  Register #(.width(32)) register_31 (.D(write_data), .en(d30), .Q(s30), .clk(clock), .clr(reset));
  Register #(.width(32)) register_32 (.D(write_data), .en(d31), .Q(s31), .clk(clock), .clr(reset));
  Multiplexer #(.select(5), .width(32), .enable("false")) multiplexer_1 (
    .in0(s1), .in1(s2), .in2(s3), .in3(s4), .in4(s5), .in5(s6), .in6(s7), .in7(s8), .in8(s9), .in9(s10),
    .in10(s11), .in11(s12), .in12(s13), .in13(s14), .in14(s15), .in15(s16), .in16(s17), .in17(s18),
    .in18(s19), .in19(s20), .in20(s21), .in21(s22), .in22(s23), .in23(s24), .in24(s25), .in25(s26),
    .in26(s27), .in27(s28), .in28(s29), .in29(s30), .in30(s31), .in31(s32), .out(read_data_1),
    .sel(read_register_1));
  Multiplexer #(.select(5), .width(32), .enable("false")) multiplexer_2 (
    .in0(s1), .in1(s2), .in2(s3), .in3(s4), .in4(s5), .in5(s6), .in6(s7), .in7(s8), .in8(s9), .in9(s10),
    .in10(s11), .in11(s12), .in12(s13), .in13(s14), .in14(s15), .in15(s16), .in16(s17), .in17(s18),
    .in18(s19), .in19(s20), .in20(s21), .in21(s22), .in22(s23), .in23(s24), .in24(s25), .in25(s26),
    .in26(s27), .in27(s28), .in28(s29), .in29(s30), .in30(s31), .in31(s32), .out(read_data_2),
    .sel(read_register_2));
endmodule

module data_memory_interface (
  input  [5:0] aluOP,
  input  [31:0] RS2,
  output [31:0] STORE_DATA
);

  wire comparator_1_eq, comparator_2_eq, comparator_3_eq, comparator_4_eq, comparator_5_eq, comparator_6_eq,
       comparator_7_eq, comparator_8_eq;
  wire [2:0] _0;
  wire [31:0] bit_extender_1_out, bit_extender_2_out, bit_extender_3_out, bit_extender_4_out,
       bit_extender_5_out, bit_extender_6_out, controlled_buffer_2_out, controlled_buffer_4_out,
       controlled_buffer_5_out, controlled_buffer_7_out, controlled_buffer_9_out, controlled_buffer_11_out,
       controlled_buffer_13_out, controlled_buffer_15_out;

  assign _0 = comparator_1_eq ? 3'b000 : 3'bz;  // Controlled_Buffer controlled_buffer_1
  Comparator #(.width(6)) comparator_1 (.a(6'b001111), .b(aluOP), .eq(comparator_1_eq));  // open: gt, lt
  assign controlled_buffer_2_out = comparator_1_eq ? RS2 : 32'bz;  // Controlled_Buffer controlled_buffer_2
  assign _0 = comparator_2_eq ? 3'b001 : 3'bz;  // Controlled_Buffer controlled_buffer_3
  Comparator #(.width(6)) comparator_2 (.a(6'b010000), .b(aluOP), .eq(comparator_2_eq));  // open: gt, lt
  assign controlled_buffer_4_out = comparator_2_eq ? RS2 : 32'bz;  // Controlled_Buffer controlled_buffer_4
  Comparator #(.width(6)) comparator_3 (.a(6'b010001), .b(aluOP), .eq(comparator_3_eq));  // open: gt, lt
  assign controlled_buffer_5_out = comparator_3_eq ? RS2 : 32'bz;  // Controlled_Buffer controlled_buffer_5
  assign _0 = comparator_4_eq ? 3'b011 : 3'bz;  // Controlled_Buffer controlled_buffer_6
  Comparator #(.width(6)) comparator_4 (.a({6{1'b0}}), .b(aluOP), .eq(comparator_4_eq));  // open: gt, lt
  assign controlled_buffer_7_out = comparator_4_eq ? RS2 : 32'bz;  // Controlled_Buffer controlled_buffer_7
  assign _0 = comparator_5_eq ? 3'b100 : 3'bz;  // Controlled_Buffer controlled_buffer_8
  Comparator #(.width(6)) comparator_5 (.a(6'b000001), .b(aluOP), .eq(comparator_5_eq));  // open: gt, lt
  assign controlled_buffer_9_out = comparator_5_eq ? RS2 : 32'bz;  // Controlled_Buffer controlled_buffer_9
  assign _0 = comparator_6_eq ? 3'b101 : 3'bz;  // Controlled_Buffer controlled_buffer_10
  Comparator #(.width(6)) comparator_6 (.a(6'b000011), .b(aluOP), .eq(comparator_6_eq));  // open: gt, lt
  assign controlled_buffer_11_out = comparator_6_eq ? RS2 : 32'bz;  // Controlled_Buffer controlled_buffer_11
  assign _0 = comparator_7_eq ? 3'b110 : 3'bz;  // Controlled_Buffer controlled_buffer_12
  Comparator #(.width(6)) comparator_7 (.a(6'b000100), .b(aluOP), .eq(comparator_7_eq));  // open: gt, lt
  assign controlled_buffer_13_out = comparator_7_eq ? RS2 : 32'bz;  // Controlled_Buffer controlled_buffer_13
  assign _0 = comparator_8_eq ? 3'b111 : 3'bz;  // Controlled_Buffer controlled_buffer_14
  Comparator #(.width(6)) comparator_8 (.a(6'b000010), .b(aluOP), .eq(comparator_8_eq));  // open: gt, lt
  assign controlled_buffer_15_out = comparator_8_eq ? RS2 : 32'bz;  // Controlled_Buffer controlled_buffer_15
  assign _0 = comparator_3_eq ? 3'b010 : 3'bz;  // Controlled_Buffer controlled_buffer_16
  assign bit_extender_1_out = {{24{1'b0}}, controlled_buffer_2_out[7:0]};  // Bit_Extender bit_extender_1
  assign bit_extender_2_out = {{16{1'b0}}, controlled_buffer_4_out[15:0]};  // Bit_Extender bit_extender_2
  assign bit_extender_3_out = {{24{controlled_buffer_7_out[7]}}, controlled_buffer_7_out[7:0]};  // Bit_Extender bit_extender_3
  assign bit_extender_4_out = {{16{controlled_buffer_9_out[15]}}, controlled_buffer_9_out[15:0]};  // Bit_Extender bit_extender_4
  assign bit_extender_5_out = {{24{1'b0}}, controlled_buffer_11_out[7:0]};  // Bit_Extender bit_extender_5
  assign bit_extender_6_out = {{16{1'b0}}, controlled_buffer_13_out[15:0]};  // Bit_Extender bit_extender_6
  // Probe on bit_extender_4_out
  // Probe on bit_extender_3_out
  // Probe on STORE_DATA
  Multiplexer #(.select(3), .width(32), .enable("false")) multiplexer_1 (
    .in0(bit_extender_1_out), .in1(bit_extender_2_out), .in2(controlled_buffer_5_out),
    .in3(bit_extender_3_out), .in4(bit_extender_4_out), .in5(bit_extender_5_out), .in6(bit_extender_6_out),
    .in7(controlled_buffer_15_out), .out(STORE_DATA), .sel(_0));
  // Probe on _0

  // Other names for the same wires on the sheet: _1[2:0] = _0; _2[2:0] = _0; _3[2:0] = _0; _4[2:0] = _0; _5[2:0] = _0;
  //   _6[2:0] = _0; _7[2:0] = _0

  // Notes on the sheet:
  //   SB
  //   SH
  //   SW
  //   LB
  //   LH
  //   LBU
  //   LHU
  //   LW
endmodule

module alu (
  input  [31:0] in_1,
  input  [5:0] ALUop,
  input  [31:0] in_3,
  input  [31:0] in_4,
  input  [31:0] in_5,
  output [31:0] out_6
);

  wire comparator_1_lt, comparator_2_lt, comparator_3_lt, comparator_4_lt, comparator_5_eq, comparator_6_eq,
       comparator_7_eq, comparator_8_eq, comparator_9_eq, comparator_10_eq, comparator_11_eq,
       comparator_12_eq, comparator_13_eq, comparator_14_eq, comparator_15_eq, comparator_16_eq,
       comparator_17_eq, comparator_18_eq, comparator_19_eq, comparator_20_eq, comparator_21_eq,
       comparator_22_eq, comparator_23_eq, comparator_24_eq, comparator_25_eq;
  wire [0:0] controlled_buffer_6_out, controlled_buffer_8_out, controlled_buffer_26_out,
       controlled_buffer_28_out;
  wire [4:0] controlled_buffer_1_out;
  wire [31:0] adder_1_out, adder_2_out, adder_3_out, and_1_out, and_2_out, controlled_buffer_2_out,
       controlled_buffer_4_out, controlled_buffer_10_out, controlled_buffer_12_out, controlled_buffer_14_out,
       controlled_buffer_16_out, controlled_buffer_18_out, controlled_buffer_20_out,
       controlled_buffer_22_out, controlled_buffer_24_out, controlled_buffer_30_out,
       controlled_buffer_32_out, controlled_buffer_34_out, controlled_buffer_36_out,
       controlled_buffer_38_out, controlled_buffer_40_out, controlled_buffer_42_out, or_1_out, or_2_out,
       shifter_1_out, shifter_2_out, shifter_3_out, shifter_4_out, shifter_5_out, shifter_6_out,
       subtractor_1_out, xor_1_out, xor_2_out;

  Adder #(.width(32)) adder_1 (.a(in_4), .b(in_5), .out(adder_1_out));  // open: cin, cout
  Adder #(.width(32)) adder_2 (.a(in_1), .b(in_4), .out(adder_2_out));  // open: cin, cout
  Shifter #(.width(32)) shifter_1 (.in(in_1), .\dist (in_4[4:0]), .out(shifter_1_out));
  Comparator #(.width(32)) comparator_1 (.a(in_1), .b(in_4), .lt(comparator_1_lt));  // open: gt, eq
  Comparator #(.width(32)) comparator_2 (.a(in_1), .b(in_4), .lt(comparator_2_lt));  // open: gt, eq
  assign xor_1_out = in_1 ^ in_4;  // XOR_Gate xor_1, 32 bits wide
  Shifter #(.width(32), .shift("lr")) shifter_2 (.in(in_1), .\dist (in_4[4:0]), .out(shifter_2_out));
  Shifter #(.width(32), .shift("ar")) shifter_3 (.in(in_1), .\dist (in_4[4:0]), .out(shifter_3_out));
  assign or_1_out = in_1 | in_4;  // OR_Gate or_1, 32 bits wide
  assign and_1_out = in_1 & in_4;  // AND_Gate and_1, 32 bits wide
  Adder #(.width(32)) adder_3 (.a(in_1), .b(in_3), .out(adder_3_out));  // open: cin, cout
  Subtractor #(.width(32)) subtractor_1 (.a(in_1), .b(in_3), .out(subtractor_1_out));  // open: bin, bout
  Shifter #(.width(32)) shifter_4 (.in(in_1), .\dist (in_3[4:0]), .out(shifter_4_out));
  Comparator #(.width(32)) comparator_3 (.a(in_1), .b(in_3), .lt(comparator_3_lt));  // open: gt, eq
  Comparator #(.width(32)) comparator_4 (.a(in_1), .b(in_3), .lt(comparator_4_lt));  // open: gt, eq
  assign xor_2_out = in_1 ^ in_3;  // XOR_Gate xor_2, 32 bits wide
  Shifter #(.width(32), .shift("lr")) shifter_5 (.in(in_1), .\dist (in_3[4:0]), .out(shifter_5_out));
  Shifter #(.width(32), .shift("ar")) shifter_6 (.in(in_1), .\dist (in_3[4:0]), .out(shifter_6_out));
  assign or_2_out = in_1 | in_3;  // OR_Gate or_2, 32 bits wide
  assign and_2_out = in_1 & in_3;  // AND_Gate and_2, 32 bits wide
  assign controlled_buffer_1_out = comparator_5_eq ? {5{1'b0}} : 5'bz;  // Controlled_Buffer controlled_buffer_1
  Comparator #(.width(6)) comparator_5 (.a(6'b000101), .b(ALUop), .eq(comparator_5_eq));  // open: gt, lt
  assign controlled_buffer_2_out = comparator_5_eq ? adder_2_out : 32'bz;  // Controlled_Buffer controlled_buffer_2
  assign controlled_buffer_1_out = comparator_6_eq ? 5'b00001 : 5'bz;  // Controlled_Buffer controlled_buffer_3
  Comparator #(.width(6)) comparator_6 (.a(6'b000110), .b(ALUop), .eq(comparator_6_eq));  // open: gt, lt
  assign controlled_buffer_4_out = comparator_6_eq ? shifter_1_out : 32'bz;  // Controlled_Buffer controlled_buffer_4
  assign controlled_buffer_1_out = comparator_7_eq ? 5'b00010 : 5'bz;  // Controlled_Buffer controlled_buffer_5
  Comparator #(.width(6)) comparator_7 (.a(6'b000111), .b(ALUop), .eq(comparator_7_eq));  // open: gt, lt
  assign controlled_buffer_6_out[0] = comparator_7_eq ? comparator_1_lt : 1'bz;  // Controlled_Buffer controlled_buffer_6
  assign controlled_buffer_1_out = comparator_8_eq ? 5'b00011 : 5'bz;  // Controlled_Buffer controlled_buffer_7
  Comparator #(.width(6)) comparator_8 (.a(6'b001000), .b(ALUop), .eq(comparator_8_eq));  // open: gt, lt
  assign controlled_buffer_8_out[0] = comparator_8_eq ? comparator_2_lt : 1'bz;  // Controlled_Buffer controlled_buffer_8
  assign controlled_buffer_1_out = comparator_9_eq ? 5'b00100 : 5'bz;  // Controlled_Buffer controlled_buffer_9
  Comparator #(.width(6)) comparator_9 (.a(6'b001001), .b(ALUop), .eq(comparator_9_eq));  // open: gt, lt
  assign controlled_buffer_10_out = comparator_9_eq ? xor_1_out : 32'bz;  // Controlled_Buffer controlled_buffer_10
  assign controlled_buffer_1_out = comparator_10_eq ? 5'b00101 : 5'bz;  // Controlled_Buffer controlled_buffer_11
  Comparator #(.width(6)) comparator_10 (.a(6'b001010), .b(ALUop), .eq(comparator_10_eq));  // open: gt, lt
  assign controlled_buffer_12_out = comparator_10_eq ? shifter_2_out : 32'bz;  // Controlled_Buffer controlled_buffer_12
  assign controlled_buffer_1_out = comparator_11_eq ? 5'b00110 : 5'bz;  // Controlled_Buffer controlled_buffer_13
  Comparator #(.width(6)) comparator_11 (.a(6'b001011), .b(ALUop), .eq(comparator_11_eq));  // open: gt, lt
  assign controlled_buffer_14_out = comparator_11_eq ? shifter_3_out : 32'bz;  // Controlled_Buffer controlled_buffer_14
  assign controlled_buffer_1_out = comparator_12_eq ? 5'b00111 : 5'bz;  // Controlled_Buffer controlled_buffer_15
  Comparator #(.width(6)) comparator_12 (.a(6'b001100), .b(ALUop), .eq(comparator_12_eq));  // open: gt, lt
  assign controlled_buffer_16_out = comparator_12_eq ? or_1_out : 32'bz;  // Controlled_Buffer controlled_buffer_16
  assign controlled_buffer_1_out = comparator_13_eq ? 5'b01000 : 5'bz;  // Controlled_Buffer controlled_buffer_17
  Comparator #(.width(6)) comparator_13 (.a(6'b001101), .b(ALUop), .eq(comparator_13_eq));  // open: gt, lt
  assign controlled_buffer_18_out = comparator_13_eq ? and_1_out : 32'bz;  // Controlled_Buffer controlled_buffer_18
  assign controlled_buffer_1_out = comparator_14_eq ? 5'b01001 : 5'bz;  // Controlled_Buffer controlled_buffer_19
  Comparator #(.width(6)) comparator_14 (.a(6'b010010), .b(ALUop), .eq(comparator_14_eq));  // open: gt, lt
  assign controlled_buffer_20_out = comparator_14_eq ? adder_3_out : 32'bz;  // Controlled_Buffer controlled_buffer_20
  assign controlled_buffer_1_out = comparator_15_eq ? 5'b01010 : 5'bz;  // Controlled_Buffer controlled_buffer_21
  Comparator #(.width(6)) comparator_15 (.a(6'b010011), .b(ALUop), .eq(comparator_15_eq));  // open: gt, lt
  assign controlled_buffer_22_out = comparator_15_eq ? subtractor_1_out : 32'bz;  // Controlled_Buffer controlled_buffer_22
  assign controlled_buffer_1_out = comparator_16_eq ? 5'b01011 : 5'bz;  // Controlled_Buffer controlled_buffer_23
  Comparator #(.width(6)) comparator_16 (.a(6'b010100), .b(ALUop), .eq(comparator_16_eq));  // open: gt, lt
  assign controlled_buffer_24_out = comparator_16_eq ? shifter_4_out : 32'bz;  // Controlled_Buffer controlled_buffer_24
  assign controlled_buffer_1_out = comparator_17_eq ? 5'b01100 : 5'bz;  // Controlled_Buffer controlled_buffer_25
  Comparator #(.width(6)) comparator_17 (.a(6'b010101), .b(ALUop), .eq(comparator_17_eq));  // open: gt, lt
  assign controlled_buffer_26_out[0] = comparator_17_eq ? comparator_3_lt : 1'bz;  // Controlled_Buffer controlled_buffer_26
  assign controlled_buffer_1_out = comparator_18_eq ? 5'b01101 : 5'bz;  // Controlled_Buffer controlled_buffer_27
  Comparator #(.width(6)) comparator_18 (.a(6'b010110), .b(ALUop), .eq(comparator_18_eq));  // open: gt, lt
  assign controlled_buffer_28_out[0] = comparator_18_eq ? comparator_4_lt : 1'bz;  // Controlled_Buffer controlled_buffer_28
  assign controlled_buffer_1_out = comparator_19_eq ? 5'b01110 : 5'bz;  // Controlled_Buffer controlled_buffer_29
  Comparator #(.width(6)) comparator_19 (.a(6'b010111), .b(ALUop), .eq(comparator_19_eq));  // open: gt, lt
  assign controlled_buffer_30_out = comparator_19_eq ? xor_2_out : 32'bz;  // Controlled_Buffer controlled_buffer_30
  assign controlled_buffer_1_out = comparator_20_eq ? 5'b01111 : 5'bz;  // Controlled_Buffer controlled_buffer_31
  Comparator #(.width(6)) comparator_20 (.a(6'b011000), .b(ALUop), .eq(comparator_20_eq));  // open: gt, lt
  assign controlled_buffer_32_out = comparator_20_eq ? shifter_5_out : 32'bz;  // Controlled_Buffer controlled_buffer_32
  assign controlled_buffer_1_out = comparator_21_eq ? 5'b10000 : 5'bz;  // Controlled_Buffer controlled_buffer_33
  Comparator #(.width(6)) comparator_21 (.a(6'b011001), .b(ALUop), .eq(comparator_21_eq));  // open: gt, lt
  assign controlled_buffer_34_out = comparator_21_eq ? shifter_6_out : 32'bz;  // Controlled_Buffer controlled_buffer_34
  assign controlled_buffer_1_out = comparator_22_eq ? 5'b10001 : 5'bz;  // Controlled_Buffer controlled_buffer_35
  Comparator #(.width(6)) comparator_22 (.a(6'b011010), .b(ALUop), .eq(comparator_22_eq));  // open: gt, lt
  assign controlled_buffer_36_out = comparator_22_eq ? or_2_out : 32'bz;  // Controlled_Buffer controlled_buffer_36
  assign controlled_buffer_1_out = comparator_23_eq ? 5'b10010 : 5'bz;  // Controlled_Buffer controlled_buffer_37
  Comparator #(.width(6)) comparator_23 (.a(6'b011011), .b(ALUop), .eq(comparator_23_eq));  // open: gt, lt
  assign controlled_buffer_38_out = comparator_23_eq ? and_2_out : 32'bz;  // Controlled_Buffer controlled_buffer_38
  assign controlled_buffer_1_out = comparator_24_eq ? 5'b10011 : 5'bz;  // Controlled_Buffer controlled_buffer_39
  Comparator #(.width(6)) comparator_24 (.a(6'b011100), .b(ALUop), .eq(comparator_24_eq));  // open: gt, lt
  assign controlled_buffer_40_out = comparator_24_eq ? {in_4[19:0], {12{1'b0}}} : 32'bz;  // Controlled_Buffer controlled_buffer_40
  assign controlled_buffer_1_out = comparator_25_eq ? 5'b10100 : 5'bz;  // Controlled_Buffer controlled_buffer_41
  Comparator #(.width(6)) comparator_25 (.a(6'b001110), .b(ALUop), .eq(comparator_25_eq));  // open: gt, lt
  assign controlled_buffer_42_out = comparator_25_eq ? {adder_1_out[19:0], {12{1'b0}}} : 32'bz;  // Controlled_Buffer controlled_buffer_42
  Multiplexer #(.select(5), .width(32), .enable("false")) multiplexer_1 (
    .in0(controlled_buffer_2_out), .in1(controlled_buffer_4_out),
    .in2({{31{1'b0}}, controlled_buffer_6_out[0]}), .in3({{31{1'b0}}, controlled_buffer_8_out[0]}),
    .in4(controlled_buffer_10_out), .in5(controlled_buffer_12_out), .in6(controlled_buffer_14_out),
    .in7(controlled_buffer_16_out), .in8(controlled_buffer_18_out), .in9(controlled_buffer_20_out),
    .in10(controlled_buffer_22_out), .in11(controlled_buffer_24_out),
    .in12({{31{1'b0}}, controlled_buffer_26_out[0]}), .in13({{31{1'b0}}, controlled_buffer_28_out[0]}),
    .in14(controlled_buffer_30_out), .in15(controlled_buffer_32_out), .in16(controlled_buffer_34_out),
    .in17(controlled_buffer_36_out), .in18(controlled_buffer_38_out), .in19(controlled_buffer_40_out),
    .in20(controlled_buffer_42_out), .out(out_6), .sel(controlled_buffer_1_out));  // open: in21, in22, in23, in24, in25, in26, in27, in28, in29, in30, in31

  // Other names for the same wires on the sheet: IMM[31:0] = in_4; PC[31:0] = in_5; RS1[31:0] = in_1;
  //   RS2[31:0] = in_3

  // Notes on the sheet:
  //   ADDI
  //   SLLI
  //   SLTI
  //   SLTIU
  //   XORI
  //   SRLI
  //   SRAI
  //   ORI
  //   ANDI
  //   ADD
  //   SUB
  //   SLL
  //   SLT
  //   SLTU
  //   XOR
  //   SRL
  //   SRA
  //   OR
  //   AND
  //   LUI
  //   AUIPC
endmodule
